// Logisim project projeto3.circ as structural Verilog: 2 circuits, main circuit main
module main (
  input  in_1
);

  wire clock_1_out;
  wire [15:0] adder_1_out, PC_q, rom_1_data;

  Adder #(.width(16)) adder_1 (.a(PC_q), .b(16'h1), .out(adder_1_out));  // open: cin, cout
  Register #(.width(16)) PC (.D(adder_1_out), .en(1'b1), .clk(clock_1_out), .Q(PC_q), .clr(in_1));
  Clock clock_1 (.out(clock_1_out));
  ROM #(.addrWidth(16), .dataWidth(16)) rom_1 (.addr(PC_q), .data(rom_1_data));
  RegistBank registbank_1 ();  // open: setValue, WriteE, R, RegistoN, ReadOut
endmodule

// NRegisto
module RegistBank (
  input  [15:0] setValue,
  input  WriteE,
  input  R,
  input  [2:0] RegistoN,
  output [15:0] ReadOut
);

  wire decoder_1_out0, decoder_1_out1, decoder_1_out2, decoder_1_out3, decoder_1_out4, decoder_1_out5,
       decoder_1_out6, decoder_1_out7;
  wire [15:0] R0_q, R1_q, R2_q, R3_q, R4_q, R5_q, R6_q, R7_q;

  Decoder #(.select(3)) decoder_1 (
    .out0(decoder_1_out0), .out1(decoder_1_out1), .out2(decoder_1_out2), .out3(decoder_1_out3),
    .out4(decoder_1_out4), .out5(decoder_1_out5), .out6(decoder_1_out6), .out7(decoder_1_out7),
    .sel(RegistoN), .en(WriteE));
  Register #(.width(16)) R0 (.D(setValue), .en(decoder_1_out0), .clk(R), .Q(R0_q));  // open: clr
  Register #(.width(16)) R1 (.D(setValue), .en(decoder_1_out1), .clk(R), .Q(R1_q));  // open: clr
  Register #(.width(16)) R2 (.D(setValue), .en(decoder_1_out2), .clk(R), .Q(R2_q));  // open: clr
  Register #(.width(16)) R3 (.D(setValue), .en(decoder_1_out3), .clk(R), .Q(R3_q));  // open: clr
  Register #(.width(16)) R4 (.D(setValue), .en(decoder_1_out4), .clk(R), .Q(R4_q));  // open: clr
  Register #(.width(16)) R5 (.D(setValue), .en(decoder_1_out5), .clk(R), .Q(R5_q));  // open: clr
  Register #(.width(16)) R6 (.D(setValue), .en(decoder_1_out6), .clk(R), .Q(R6_q));  // open: clr
  Register #(.width(16)) R7 (.D(setValue), .en(decoder_1_out7), .clk(R), .Q(R7_q));  // open: clr
  Multiplexer #(.select(3), .width(16)) multiplexer_1 (
    .in0(R0_q), .in1(R1_q), .in2(R2_q), .in3(R3_q), .in4(R4_q), .in5(R5_q), .in6(R6_q), .in7(R7_q),
    .out(ReadOut), .sel(RegistoN));
endmodule
